# Fritzing sketch meteo (saved by Fritzing 0.9.3b)
circuit board: 8.46667cm x 5.64444cm
breadboards: 1

parts:
  LCD1 = LCD screen
  Part1 = Arduino Uno (Rev3)
  R1 = Rotary Potentiometer (Small) [maximum_resistance=10kΩ package=THT]
  Part2 = Adafruit BMP180
  DHT1 = DHT11 Humitidy and Temperature Sensor
  S1 = Pushbutton [package="[THT]"]

nets:
  GND: LCD1.VSS, LCD1.R/W, LCD1.LED-, Part1.GND, R1.leg1, Part2.GND, DHT1.GND
  VDD: LCD1.VDD, LCD1.LED+, Part1.5V, R1.leg2, S1.Pin_3, S1.Pin_4
  N1: LCD1.V0, R1.wiper
  N2: LCD1.RS, Part1.D7
  N3: LCD1.E, Part1.D8
  N4: LCD1.DB4, Part1.D9_PWM
  N5: LCD1.DB5, Part1.D10_PWM/SS
  N6: LCD1.DB6, Part1.D11_PWM/MOSI
  N7: LCD1.DB7, Part1.D12/MISO
  N8: Part1.A4/SDA, Part2.SDA
  N9: Part1.A5/SCL, Part2.SCL
  N10: Part1.D4, S1.Pin_1, S1.Pin_2
  N11: Part1.D5_PWM, DHT1.DATA
  3V3: Part1.3V3, Part2.+3V3, DHT1.VDD

custom parts:
  Adafruit BMP180: This precision sensor from Bosch is the best low-cost sensing solution for measuring barometric pressure and temperature. Because pressure changes with altitude you can also use it as an altimeter! The sensor is soldered onto a PCB with a 3.3V regulator, I2C level shifter and pull-up resistors on the I2C pins. The BMP180 is the next-generation of sensors from Bosch, and replaces the BMP085.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
  DHT11 Humitidy and Temperature Sensor: DHT11 Humidity and Temperature Sensor
